# Fritzing sketch schematic (saved by Fritzing 1.0.4)
breadboards: 1

parts:
  Part1 = Arduino Uno (Rev3) - ICSP
  J1 = Basic Servo
  DotStar2 = DorStar LED Strip [part_number=2239]
  JACK2 = 2.1mm Barrel Jack with Terminal Block
  Sensor1 = Gas Sensor Breakout Board

nets:
  N1: Part1.A0, Sensor1.AOUT
  N2: Part1.D2, DotStar2.DI
  N3: Part1.D3_PWM, DotStar2.CI
  N4: Part1.D6_PWM, J1.pulse
  5V: Part1.5V, J1.vcc, Sensor1.5V
  GND: Part1.GND, J1.gnd, DotStar2.GND, Sensor1.GND
  N5: DotStar2.+5V, JACK2.POS

notes:
  Gas sensor
  MQ-135
  Power Supply
  5V

custom parts:
  DorStar LED Strip: DotStar LED strip, black, 60 LEDs/m
  Gas Sensor Breakout Board: Gas sensor breakout board. Input voltage is 5V. Sensor output is available in analog and digital.
